# Fritzing sketch RPi_LIS3DH (saved by Fritzing 0.9.2b)
breadboards: 1

parts:
  LIS3DH = Adafruit LIS3DH [part_number="Adafruit #2809"]
  Raspberry_Pi_3 = Raspberry Pi 3

nets:
  3V3: LIS3DH.VIN, Raspberry_Pi_3.3v3, Raspberry_Pi_3.3V3
  GND: LIS3DH.GND, LIS3DH.CS, Raspberry_Pi_3.GND
  N1: LIS3DH.SCL, Raspberry_Pi_3.GIPO11
  N2: LIS3DH.SDA, Raspberry_Pi_3.GIPO10
  N3: LIS3DH.SDO, Raspberry_Pi_3.GIPO9

custom parts:
  Adafruit LIS3DH: The LIS3DH is a very popular low power triple-axis accelerometer. It's low-cost, but has just about every 'extra' you'd want in an accelerometer: Three axis sensing, 10-bit precision ±2g/±4g/±8g/±16g selectable scaling Both I2C (2 possible addresses) and SPI interface options Interrupt output Multiple data rate options 1 Hz to 5Khz As low as 2uA current draw (just the chip itself, not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
